// Logisim project datapath.circ as structural Verilog: 1 circuit, main circuit main
module main (
  input  [1:0] PLAYER1,
  input  [1:0] PLAYER2,
  input  START,
  input  in_4,
  output [4:0] out_5
);

  wire and_1_out, and_2_out, and_3_out, and_4_out, clock_1_out, clock_2_out, comparator_1_eq,
       comparator_2_eq, comparator_3_eq, comparator_4_eq, comparator_5_eq, comparator_6_eq, comparator_7_eq,
       comparator_8_eq, comparator_9_eq, comparator_10_gt, comparator_11_eq, comparator_12_eq, nor_1_out,
       not_1_out, or_1_out, or_2_out;
  wire [1:0] demultiplexer_1_out1, demultiplexer_2_out1, multiplexer_2_out, multiplexer_3_out,
       multiplexer_5_out, undriven;
  wire [4:0] adder_1_out, adder_2_out, adder_3_out, adder_4_out, ADVANTAGE_REGISTER_q, MANCHE_COUNT_q,
       multiplexer_1_out, multiplexer_4_out, multiplexer_6_out, multiplexer_7_out, multiplexer_8_out,
       multiplexer_9_out, multiplexer_10_out, subtractor_1_out;

  Demultiplexer #(.width(2)) demultiplexer_1 (.out1(demultiplexer_1_out1), .in(PLAYER1), .sel(START));  // open: out0
  Comparator #(.mode("unsigned"), .width(2)) comparator_1 (
    .a(demultiplexer_1_out1), .b(2'b01), .eq(comparator_1_eq));  // open: gt, lt
  Comparator #(.mode("unsigned"), .width(2)) comparator_2 (
    .a(demultiplexer_2_out1), .b(2'b11), .eq(comparator_2_eq));  // open: gt, lt
  and and_1 (and_1_out, comparator_1_eq, comparator_2_eq);
  Demultiplexer #(.width(2)) demultiplexer_2 (.out1(demultiplexer_2_out1), .in(PLAYER2), .sel(START));  // open: out0
  Comparator #(.mode("unsigned"), .width(2)) comparator_3 (
    .a(demultiplexer_1_out1), .b(2'b10), .eq(comparator_3_eq));  // open: gt, lt
  Comparator #(.mode("unsigned"), .width(2)) comparator_4 (
    .a(demultiplexer_2_out1), .b(2'b01), .eq(comparator_4_eq));  // open: gt, lt
  and and_2 (and_2_out, comparator_3_eq, comparator_4_eq);
  or or_1 (or_1_out, and_1_out, and_2_out, and_3_out);
  Multiplexer #(.select(2), .width(5)) multiplexer_1 (
    .in0({5{1'b0}}), .in1(5'b00100), .in2(5'b01000), .in3(5'b01100), .out(multiplexer_1_out),
    .sel(demultiplexer_1_out1));
  Multiplexer #(.width(2)) multiplexer_2 (.in0(2'b10), .in1(2'b01), .out(multiplexer_2_out), .sel(or_1_out));
  Clock clock_1 (.out(clock_1_out));
  Comparator #(.mode("unsigned"), .width(2)) comparator_5 (
    .a(demultiplexer_1_out1), .b(2'b11), .eq(comparator_5_eq));  // open: gt, lt
  Multiplexer #(.width(2)) multiplexer_3 (
    .in0(multiplexer_2_out), .in1(2'b00), .out(multiplexer_3_out), .sel(or_2_out));
  Multiplexer #(.select(2), .width(5)) multiplexer_4 (
    .in0({5{1'b0}}), .in1(5'b00001), .in2(5'b00010), .in3(5'b00011), .out(multiplexer_4_out),
    .sel(demultiplexer_2_out1));
  Adder #(.width(5)) adder_1 (.a(multiplexer_4_out), .b(multiplexer_1_out), .out(adder_1_out));  // open: cin, cout
  Comparator #(.mode("unsigned"), .width(2)) comparator_6 (
    .a(demultiplexer_2_out1), .b(2'b10), .eq(comparator_6_eq));  // open: gt, lt
  and and_3 (and_3_out, comparator_5_eq, comparator_6_eq);
  Multiplexer #(.width(2)) multiplexer_5 (
    .in0(multiplexer_3_out), .in1(2'b11), .out(multiplexer_5_out), .sel(and_4_out));
  Adder #(.width(5)) adder_2 (.a(adder_1_out), .b(5'b00100), .out(adder_2_out));  // open: cin, cout
  Comparator #(.mode("unsigned"), .width(2)) comparator_7 (
    .a(demultiplexer_1_out1), .b(2'b00), .eq(comparator_7_eq));  // open: gt, lt
  Comparator #(.mode("unsigned"), .width(2)) comparator_8 (
    .a(demultiplexer_2_out1), .b(2'b00), .eq(comparator_8_eq));  // open: gt, lt
  or or_2 (or_2_out, comparator_7_eq, comparator_8_eq);
  Register #(.width(5)) MAX_MANCHE (.D(adder_2_out), .Q(out_5), .clk(clock_1_out));  // open: en, clr
  not not_1 (not_1_out, or_2_out);
  and and_4 (and_4_out, not_1_out, comparator_9_eq);
  Comparator #(.mode("unsigned"), .width(2)) comparator_9 (
    .a(demultiplexer_2_out1), .b(demultiplexer_1_out1), .eq(comparator_9_eq));  // open: gt, lt
  Comparator #(.mode("unsigned"), .width(2)) comparator_10 (
    .a(undriven), .b(2'b00), .gt(comparator_10_gt));  // open: eq, lt
  Comparator #(.mode("unsigned"), .width(2)) comparator_11 (
    .a(undriven), .b(2'b00), .eq(comparator_11_eq));  // open: gt, lt
  Comparator #(.mode("unsigned"), .width(2)) comparator_12 (
    .a(undriven), .b(2'b11), .eq(comparator_12_eq));  // open: gt, lt
  nor nor_1 (nor_1_out, comparator_11_eq, comparator_12_eq);
  Adder #(.width(5)) adder_3 (.a(multiplexer_6_out), .b(ADVANTAGE_REGISTER_q), .out(adder_3_out));  // open: cin, cout
  Subtractor #(.width(5)) subtractor_1 (
    .a(ADVANTAGE_REGISTER_q), .b(multiplexer_6_out), .out(subtractor_1_out));  // open: bin, bout
  Multiplexer #(.width(5)) multiplexer_6 (.in0({5{1'b0}}), .in1(5'b00001), .out(multiplexer_6_out), .sel(nor_1_out));
  Multiplexer #(.select(2), .width(5)) multiplexer_7 (
    .in0(ADVANTAGE_REGISTER_q), .in1(subtractor_1_out), .in2(adder_3_out), .in3(ADVANTAGE_REGISTER_q),
    .out(multiplexer_7_out), .sel(undriven));
  Multiplexer #(.width(5)) multiplexer_8 (.in0(multiplexer_7_out), .in1(5'b00010), .out(multiplexer_8_out), .sel(in_4));
  Multiplexer #(.width(5)) multiplexer_9 (
    .in0({5{1'b0}}), .in1(5'b00001), .out(multiplexer_9_out), .sel(comparator_10_gt));
  Register #(.width(5)) MANCHE_COUNT (.D(multiplexer_10_out), .Q(MANCHE_COUNT_q), .clk(clock_2_out));  // open: en, clr
  Adder #(.width(5)) adder_4 (.a(multiplexer_9_out), .b(MANCHE_COUNT_q), .out(adder_4_out));  // open: cin, cout
  Multiplexer #(.width(5)) multiplexer_10 (.in0(adder_4_out), .in1({5{1'b0}}), .out(multiplexer_10_out), .sel(in_4));
  Register #(.width(5)) ADVANTAGE_REGISTER (
    .D(multiplexer_8_out), .Q(ADVANTAGE_REGISTER_q), .clk(clock_2_out));  // open: en, clr
  Clock clock_2 (.out(clock_2_out));
endmodule
