// Logisim project new_datapath.circ as structural Verilog: 6 circuits, main circuit main
module main (
  input  [1:0] P1_MOVE,
  input  [1:0] P2_MOVE,
  input  START,
  output [4:0] TOTAL,
  output [1:0] WINNING_PLAYER,
  output [4:0] PLD,
  output ENDABLE,
  output W1,
  output W2,
  output D
);

  wire and_1_out, comparator_1_gt, comparator_2_eq, comparator_3_gt, or_1_out, undriven_3, undriven_4,
       undriven_5;
  wire [4:0] undriven, undriven_2;

  match_winner match_winner_1 ();  // open: P1, P2, PW_TMP, START, W1, W2, D, NUL
  tmp_winner tmp_winner_1 ();  // open: P1_MOVE, P2_MOVE, PW_TMP
  match_winner match_winner_2 ();  // open: P1, P2, PW_TMP, START, W1, W2, D, NUL
  set_total_manche set_total_manche_1 ();  // open: START, P1_MOVE, P2_MOVE, TO_PLAY
  Clock CLK ();  // open: out
  game_count game_count_1 ();  // open: START, INVALID, PLAYED_MATCH
  Comparator #(.width(5)) comparator_1 (.a(PLD), .b(5'b00011), .gt(comparator_1_gt));  // open: eq, lt
  Comparator #(.width(5)) comparator_2 (.a(undriven), .b(PLD), .eq(comparator_2_eq));  // open: gt, lt
  or or_1 (or_1_out, comparator_1_gt, comparator_2_eq);
  Comparator #(.width(5)) comparator_3 (.a(undriven_2), .b(5'b00001), .gt(comparator_3_gt));  // open: eq, lt
  and and_1 (and_1_out, comparator_3_gt, comparator_1_gt);
  or or_2 (ENDABLE, and_1_out, comparator_2_eq);
  and and_2 (W1, undriven_5, or_1_out);
  and and_3 (W2, undriven_4, or_1_out);
  and and_4 (D, or_1_out, undriven_3);

  // Notes on the sheet:
  //   END GAME
  //   O: w1
  //   O: w2
  //   O: d
  //   O: endable
  //   NOTE:
  //   1 manca il controllo sulla mossa precedente
  //   2 la logica winning manche sara' riassunta con una logica combinatoria personalizzata
  //   3 la logica total manche sara' riassunta con una logica combinatoria personalizzata
endmodule

module tmp_winner (
  input  [1:0] P1_MOVE,
  input  [1:0] P2_MOVE,
  output [1:0] PW_TMP
);

  wire and_1_out, and_2_out, and_3_out, and_4_out, comparator_1_eq, comparator_2_eq, comparator_3_eq,
       comparator_4_eq, comparator_5_eq, comparator_6_eq, comparator_7_eq, comparator_8_eq, comparator_9_eq,
       not_1_out, or_1_out, or_2_out;
  wire [1:0] multiplexer_1_out, multiplexer_2_out;

  Comparator #(.mode("unsigned"), .width(2)) comparator_1 (
    .a(P2_MOVE), .b(2'b01), .eq(comparator_1_eq));  // open: gt, lt
  Comparator #(.mode("unsigned"), .width(2)) comparator_2 (
    .a(P1_MOVE), .b(2'b11), .eq(comparator_2_eq));  // open: gt, lt
  and and_1 (and_1_out, comparator_1_eq, comparator_2_eq);
  Comparator #(.mode("unsigned"), .width(2)) comparator_3 (
    .a(P2_MOVE), .b(2'b10), .eq(comparator_3_eq));  // open: gt, lt
  Comparator #(.mode("unsigned"), .width(2)) comparator_4 (
    .a(P1_MOVE), .b(2'b01), .eq(comparator_4_eq));  // open: gt, lt
  and and_2 (and_2_out, comparator_3_eq, comparator_4_eq);
  or or_1 (or_1_out, and_1_out, and_2_out, and_3_out);
  Multiplexer #(.width(2)) multiplexer_1 (.in0(2'b10), .in1(2'b01), .out(multiplexer_1_out), .sel(or_1_out));
  Multiplexer #(.width(2)) multiplexer_2 (
    .in0(multiplexer_1_out), .in1(2'b00), .out(multiplexer_2_out), .sel(or_2_out));
  Comparator #(.mode("unsigned"), .width(2)) comparator_5 (
    .a(P2_MOVE), .b(2'b11), .eq(comparator_5_eq));  // open: gt, lt
  Multiplexer #(.width(2)) multiplexer_3 (.in0(multiplexer_2_out), .in1(2'b11), .out(PW_TMP), .sel(and_4_out));
  Comparator #(.mode("unsigned"), .width(2)) comparator_6 (
    .a(P1_MOVE), .b(2'b10), .eq(comparator_6_eq));  // open: gt, lt
  and and_3 (and_3_out, comparator_5_eq, comparator_6_eq);
  Comparator #(.mode("unsigned"), .width(2)) comparator_7 (
    .a(P2_MOVE), .b(2'b00), .eq(comparator_7_eq));  // open: gt, lt
  or or_2 (or_2_out, comparator_7_eq, comparator_8_eq);
  Comparator #(.mode("unsigned"), .width(2)) comparator_8 (
    .a(P1_MOVE), .b(2'b00), .eq(comparator_8_eq));  // open: gt, lt
  not not_1 (not_1_out, or_2_out);
  and and_4 (and_4_out, not_1_out, comparator_9_eq);
  Comparator #(.mode("unsigned"), .width(2)) comparator_9 (
    .a(P1_MOVE), .b(P2_MOVE), .eq(comparator_9_eq));  // open: gt, lt
endmodule

module set_total_manche (
  input  START,
  input  [1:0] P1_MOVE,
  input  [1:0] P2_MOVE,
  output [4:0] TO_PLAY
);

  wire adder_1_cout, clock_1_out;
  wire [4:0] adder_1_out, adder_2_out, multiplexer_1_out, multiplexer_2_out, multiplexer_3_out;

  Clock clock_1 (.out(clock_1_out));
  Multiplexer #(.select(2), .width(5)) multiplexer_1 (
    .in0({5{1'b0}}), .in1(5'b00100), .in2(5'b01000), .in3(5'b01100), .out(multiplexer_1_out), .sel(P1_MOVE));
  Adder #(.width(5)) adder_1 (
    .a(multiplexer_2_out), .b(multiplexer_1_out), .out(adder_1_out), .cout(adder_1_cout));  // open: cin
  Multiplexer #(.select(2), .width(5)) multiplexer_2 (
    .in0({5{1'b0}}), .in1(5'b00001), .in2(5'b00010), .in3(5'b00011), .out(multiplexer_2_out), .sel(P2_MOVE));
  Adder #(.width(5)) adder_2 (.a(adder_1_out), .b(5'b00100), .out(adder_2_out));  // open: cin, cout
  Multiplexer #(.width(5)) multiplexer_3 (.in0(TO_PLAY), .in1(adder_2_out), .out(multiplexer_3_out), .sel(START));
  Register #(.width(5)) FINAL (.D(multiplexer_3_out), .Q(TO_PLAY), .clk(clock_1_out));  // open: en, clr
endmodule

module game_count (
  input  START,
  input  INVALID,
  output [4:0] PLAYED_MATCH
);

  wire clock_1_out;
  wire [4:0] adder_1_out, multiplexer_1_out, multiplexer_2_out;

  Clock clock_1 (.out(clock_1_out));
  Adder #(.width(5)) adder_1 (.a(PLAYED_MATCH), .b(5'b00001), .out(adder_1_out));  // open: cin, cout
  Multiplexer #(.width(5)) multiplexer_1 (
    .in0(adder_1_out), .in1(PLAYED_MATCH), .out(multiplexer_1_out), .sel(INVALID));
  Multiplexer #(.width(5)) multiplexer_2 (
    .in0(multiplexer_1_out), .in1({5{1'b0}}), .out(multiplexer_2_out), .sel(START));
  Register #(.width(5)) PLAYED (.D(multiplexer_2_out), .Q(PLAYED_MATCH), .clk(clock_1_out));  // open: en, clr
endmodule

module match_winner (
  input  [1:0] P1,
  input  [1:0] P2,
  input  [1:0] PW_TMP,
  input  START,
  output W1,
  output W2,
  output D,
  output NUL
);

  wire clock_1_out, comparator_1_eq, comparator_2_eq, comparator_3_eq, comparator_4_eq, comparator_5_eq,
       nor_1_out, or_1_out, WIN1_out, WIN2_out;
  wire [1:0] multiplexer_1_out, multiplexer_2_out, multiplexer_3_out, multiplexer_4_out, multiplexer_5_out,
       PREV_WM_q, PREV_WP_q;

  Clock clock_1 (.out(clock_1_out));
  Comparator #(.mode("unsigned"), .width(2)) comparator_1 (
    .a(PW_TMP), .b(2'b01), .eq(comparator_1_eq));  // open: gt, lt
  Comparator #(.mode("unsigned"), .width(2)) comparator_2 (
    .a(PW_TMP), .b(2'b10), .eq(comparator_2_eq));  // open: gt, lt
  Comparator #(.mode("unsigned"), .width(2)) comparator_3 (
    .a(PW_TMP), .b(2'b11), .eq(comparator_3_eq));  // open: gt, lt
  Comparator #(.mode("unsigned"), .width(2)) comparator_4 (
    .a(PW_TMP), .b(2'b00), .eq(comparator_4_eq));  // open: gt, lt
  Multiplexer #(.select(2), .width(2)) multiplexer_1 (
    .in0(PREV_WM_q), .in1(P1), .in2(P2), .in3(2'b00), .out(multiplexer_1_out), .sel(PW_TMP));
  Multiplexer #(.select(2), .width(2)) multiplexer_2 (
    .in0(PREV_WP_q), .in1(PW_TMP), .in2(PW_TMP), .in3(2'b00), .out(multiplexer_2_out), .sel(PW_TMP));
  nor nor_1 (nor_1_out, comparator_3_eq, comparator_4_eq);
  Multiplexer #(.width(2)) multiplexer_3 (.in0(multiplexer_1_out), .in1(2'b00), .out(multiplexer_3_out), .sel(START));
  Multiplexer #(.width(2)) multiplexer_4 (.in0(multiplexer_2_out), .in1(2'b00), .out(multiplexer_4_out), .sel(START));
  Register #(.width(2)) PREV_WM (.D(multiplexer_3_out), .Q(PREV_WM_q), .clk(clock_1_out));  // open: en, clr
  Register #(.width(2)) PREV_WP (.D(multiplexer_4_out), .Q(PREV_WP_q), .clk(clock_1_out));  // open: en, clr
  and WIN1 (WIN1_out, comparator_1_eq, nor_1_out);
  and WIN2 (WIN2_out, comparator_2_eq, nor_1_out);
  Multiplexer #(.select(2), .width(2)) multiplexer_5 (
    .in0(2'b00), .in1(P1), .in2(P2), .in3(P1), .out(multiplexer_5_out), .sel(PREV_WP_q));
  Comparator #(.mode("unsigned"), .width(2)) comparator_5 (
    .a(PREV_WM_q), .b(multiplexer_5_out), .eq(comparator_5_eq));  // open: gt, lt
  or or_1 (or_1_out, comparator_4_eq, comparator_5_eq);
  Multiplexer multiplexer_6 (.in0(WIN1_out), .in1(1'b0), .out(W1), .sel(START));
  Multiplexer multiplexer_7 (.in0(WIN2_out), .in1(1'b0), .out(W2), .sel(START));
  Multiplexer multiplexer_8 (.in0(comparator_3_eq), .in1(1'b0), .out(D), .sel(START));
  Multiplexer multiplexer_9 (.in0(or_1_out), .in1(1'b0), .out(NUL), .sel(START));

  // Notes on the sheet:
  //   draw
  //   invalid
endmodule

module game_adv (
);

  wire comparator_1_gt, comparator_2_eq, nor_1_out, undriven, undriven_2, undriven_3, undriven_4, undriven_5,
       undriven_6, undriven_7, undriven_8;
  wire [4:0] adder_1_out, adder_2_out, adder_3_out, adder_4_out, COUNT_1_q, COUNT_2_q, multiplexer_1_out,
       multiplexer_2_out, multiplexer_3_out, multiplexer_4_out, multiplexer_5_out, multiplexer_6_out,
       multiplexer_7_out, multiplexer_8_out, multiplexer_9_out, multiplexer_10_out, multiplexer_11_out,
       multiplexer_12_out, subtractor_1_out, subtractor_2_out, WCOUNT_1_q, WCOUNT_2_q;

  Adder #(.width(5)) adder_1 (.a(WCOUNT_1_q), .b(5'b00001), .out(adder_1_out));  // open: cin, cout
  Adder #(.width(5)) adder_2 (.a(WCOUNT_2_q), .b(5'b00001), .out(adder_2_out));  // open: cin, cout
  Multiplexer #(.width(5)) multiplexer_1 (
    .in0(WCOUNT_1_q), .in1(adder_1_out), .out(multiplexer_1_out), .sel(undriven_2));
  Multiplexer #(.width(5)) multiplexer_2 (
    .in0(multiplexer_1_out), .in1({5{1'b0}}), .out(multiplexer_2_out), .sel(undriven_3));
  Multiplexer #(.width(5)) multiplexer_3 (
    .in0(multiplexer_2_out), .in1(WCOUNT_1_q), .out(multiplexer_3_out), .sel(undriven));
  Multiplexer #(.width(5)) multiplexer_4 (
    .in0(WCOUNT_2_q), .in1(adder_2_out), .out(multiplexer_4_out), .sel(undriven_2));
  Multiplexer #(.width(5)) multiplexer_5 (
    .in0(multiplexer_4_out), .in1({5{1'b0}}), .out(multiplexer_5_out), .sel(undriven_3));
  Multiplexer #(.width(5)) multiplexer_6 (
    .in0(multiplexer_5_out), .in1(WCOUNT_2_q), .out(multiplexer_6_out), .sel(undriven));
  Register #(.width(5)) WCOUNT_1 (.D(multiplexer_3_out), .Q(WCOUNT_1_q));  // open: en, clk, clr
  Register #(.width(5)) WCOUNT_2 (.D(multiplexer_6_out), .Q(WCOUNT_2_q));  // open: en, clk, clr
  Multiplexer #(.width(5)) multiplexer_7 (
    .in0(COUNT_1_q), .in1(adder_3_out), .out(multiplexer_7_out), .sel(undriven_4));
  Multiplexer #(.width(5)) multiplexer_8 (
    .in0(multiplexer_7_out), .in1({5{1'b0}}), .out(multiplexer_8_out), .sel(undriven_6));
  Multiplexer #(.width(5)) multiplexer_9 (
    .in0(multiplexer_8_out), .in1(COUNT_1_q), .out(multiplexer_9_out), .sel(undriven_7));
  Adder #(.width(5)) adder_3 (.a(COUNT_1_q), .b(5'b00001), .out(adder_3_out));  // open: cin, cout
  Register #(.width(5)) COUNT_1 (.D(multiplexer_9_out), .Q(COUNT_1_q), .clk(undriven_8));  // open: en, clr
  Multiplexer #(.width(5)) multiplexer_10 (
    .in0(COUNT_2_q), .in1(adder_4_out), .out(multiplexer_10_out), .sel(undriven_5));
  Multiplexer #(.width(5)) multiplexer_11 (
    .in0(multiplexer_10_out), .in1({5{1'b0}}), .out(multiplexer_11_out), .sel(undriven_6));
  Multiplexer #(.width(5)) multiplexer_12 (
    .in0(multiplexer_11_out), .in1(COUNT_2_q), .out(multiplexer_12_out), .sel(undriven_7));
  Adder #(.width(5)) adder_4 (.a(COUNT_2_q), .b(5'b00001), .out(adder_4_out));  // open: cin, cout
  Register #(.width(5)) COUNT_2 (.D(multiplexer_12_out), .Q(COUNT_2_q), .clk(undriven_8));  // open: en, clr
  Comparator #(.mode("unsigned"), .width(5)) comparator_1 (
    .a(COUNT_1_q), .b(COUNT_2_q), .gt(comparator_1_gt));  // open: eq, lt
  Comparator #(.mode("unsigned"), .width(5)) comparator_2 (
    .a(COUNT_2_q), .b(COUNT_1_q), .eq(comparator_2_eq));  // open: gt, lt
  nor nor_1 (nor_1_out, comparator_1_gt, comparator_2_eq);
  Subtractor #(.width(5)) subtractor_1 (.a(COUNT_1_q), .b(COUNT_2_q), .out(subtractor_1_out));  // open: bin, bout
  Subtractor #(.width(5)) subtractor_2 (.a(COUNT_2_q), .b(COUNT_1_q), .out(subtractor_2_out));  // open: bin, bout
  Multiplexer #(.width(5)) multiplexer_13 (
    .in0(subtractor_2_out), .in1(subtractor_1_out), .sel(comparator_1_gt));  // open: out

  // Notes on the sheet:
  //   I: w1
  //   I: start
  //   I: d
endmodule
